// Logisim project FastClockSwitching.circ as structural Verilog: 1 circuit, main circuit main
module main (
  input  [1:0] Data
);

  wire and_1_out, and_2_out, and_3_out, CLK_CS_out, d_ff_1_q, d_ff_2_q, MHz2_out, MHz4_out, MHz8_out, MR_out,
       multiplexer_1_out, not_1_out, not_2_out, not_3_out;
  wire [1:0] register_1_q;

  Button #(.press("passive")) CLK_CS (.out(CLK_CS_out));
  not not_1 (not_1_out, CLK_CS_out);
  Button MR (.out(MR_out));
  and and_1 (and_1_out, not_1_out, MHz8_out);
  Clock #(.highDuration(2), .lowDuration(2)) MHz4 (.out(MHz4_out));
  Clock MHz8 (.out(MHz8_out));
  Register #(.width(2)) register_1 (.D(Data), .en(1'b1), .clk(not_2_out), .Q(register_1_q), .clr(MR_out));
  not not_2 (not_2_out, and_1_out);
  Clock #(.highDuration(4), .lowDuration(4)) MHz2 (.out(MHz2_out));
  Multiplexer #(.select(2)) multiplexer_1 (
    .in0(MHz2_out), .in1(MHz4_out), .in2(MHz8_out), .in3(MHz8_out), .out(multiplexer_1_out),
    .sel(register_1_q));
  not not_3 (not_3_out, multiplexer_1_out);
  and and_2 (and_2_out, d_ff_1_q, not_2_out);
  and and_3 (and_3_out, d_ff_2_q, multiplexer_1_out);
  D_Flip_Flop d_ff_1 (.D(not_2_out), .clk(not_3_out), .Q(d_ff_1_q), .preset(1'b0), .reset(and_1_out));  // open: Qn
  D_Flip_Flop d_ff_2 (.D(and_2_out), .clk(not_3_out), .Q(d_ff_2_q), .preset(1'b0), .reset(and_1_out));  // open: Qn
  LED led_1 (.in(and_3_out));
endmodule
