// Logisim project Speed_RGB_LED.circ as structural Verilog: 2 circuits, main circuit main
module main (
  input  Computer_D0
);

  wire clock_1_out, clock_2_out, Computer_CS_out, d_ff_1_q, MR_out, multiplexer_1_out, not_1_out;

  Button Computer_CS (.out(Computer_CS_out));
  Button MR (.out(MR_out));
  D_Flip_Flop d_ff_1 (.D(Computer_D0), .clk(Computer_CS_out), .Q(d_ff_1_q), .preset(1'b0), .reset(MR_out));  // open: Qn
  Clock clock_1 (.out(clock_1_out));
  Clock #(.highDuration(3), .lowDuration(3)) clock_2 (.out(clock_2_out));
  Multiplexer multiplexer_1 (.in0(clock_1_out), .in1(clock_2_out), .out(multiplexer_1_out), .sel(d_ff_1_q));
  not not_1 (not_1_out, multiplexer_1_out);
  // AND_Gate and_1 has open pins: in1=Computer_CS_out, out=open
  D_Flip_Flop d_ff_2 (.clk(not_1_out));  // open: D, Q, Qn, preset, reset
  D_Flip_Flop d_ff_3 ();  // open: D, clk, Q, Qn, preset, reset
endmodule

module TURBO2 (
  input  CLK,
  input  CPU,
  input  TOG,
  output D
);

  wire nand_1_out, nand_2_out, nand_3_out;

  nand nand_1 (nand_1_out, 1'b1, CLK);
  nand nand_2 (nand_2_out, nand_1_out, TOG);
  nand nand_3 (nand_3_out, CLK, CPU);
  nand nand_4 (D, nand_2_out, nand_3_out);
endmodule
