// Logisim project SimulateGlueLogic.circ as structural Verilog: 1 circuit, main circuit main
module main (
  input  nIOREQ,
  input  nWR,
  input  nRD,
  input  nMREQ,
  input  A15
);

  wire button_1_out, button_2_out, nand_1_out, nand_2_out, or_1_out, or_2_out, or_3_out, or_4_out, or_5_out,
       or_6_out, or_7_out;

  or or_1 (or_1_out, nIOREQ, nWR);
  Button #(.press("passive")) button_1 (.out(button_1_out));
  or or_2 (or_2_out, nIOREQ, nRD);
  or or_3 (or_3_out, nMREQ, nWR);
  or or_4 (or_4_out, nMREQ, nRD);
  Button #(.press("passive")) button_2 (.out(button_2_out));
  LED led_1 (.in(or_1_out));
  or or_5 (or_5_out, or_1_out, button_1_out);
  LED led_2 (.in(or_2_out));
  LED led_3 (.in(or_3_out));
  LED led_4 (.in(or_4_out));
  nand nand_1 (nand_1_out, button_2_out, nand_2_out);
  nand nand_2 (nand_2_out, nand_1_out, or_5_out);
  or or_6 (or_6_out, nand_1_out, or_4_out);
  LED led_5 (.in(or_6_out));
  or or_7 (or_7_out, or_4_out, nand_2_out);
  LED led_6 (.in(or_7_out));

  // Notes on the sheet:
  //   A15: pull=up
  //   nIOREQ: pull=up
  //   nWR: pull=up
  //   nRD: pull=up
  //   nMREQ: pull=up
  //   /RESET
  //   /IOWR
  //   /IO 30h
  //   /IORD
  //   /MEMWR
  //   /MEMRD
  //   /DIS_ROM
  //   DIS_ROM
  //   /RAM_OE
  //   /ROM_CS
endmodule
